# Fritzing sketch version2 (saved by Fritzing 0.9.3b)
circuit board: 6.88566cm x 5.36311cm
breadboards: 1

parts:
  Part1 = Arduino Uno (Rev3)
  R7 = Resistor [tolerance=±5% resistance=470 package=THT]
  R8 = Resistor [tolerance=±5% resistance=470 package=THT]
  R9 = Resistor [tolerance=±5% resistance=470 package=THT]
  LED1 = RGB LED (com. cathode, rgb) [package="5 mm [THT]"]
  LED2 = RGB LED (com. cathode, rgb) [package="5 mm [THT]"]
  LED3 = RGB LED (com. cathode, rgb) [package="5 mm [THT]"]
  R10 = Resistor [tolerance=±5% resistance=470 package=THT]
  LED4 = RGB LED (com. cathode, rgb) [package="5 mm [THT]"]
  LED5 = RGB LED (com. cathode, rgb) [package="5 mm [THT]"]
  LED6 = RGB LED (com. cathode, rgb) [package="5 mm [THT]"]
  R11 = Resistor [tolerance=±5% resistance=470 package=THT]
  LED7 = RGB LED (com. cathode, rgb) [package="5 mm [THT]"]
  LED8 = RGB LED (com. cathode, rgb) [package="5 mm [THT]"]
  LED9 = RGB LED (com. cathode, rgb) [package="5 mm [THT]"]
  R12 = Resistor [tolerance=±5% resistance=470 package=THT]
  R13 = Resistor [tolerance=±5% resistance=470 package=THT]
  R14 = Resistor [tolerance=±5% resistance=470 package=THT]
  R15 = Resistor [tolerance=±5% resistance=470 package=THT]
  J1 = female pin header, 5 pins [form="♀ (female)"]

nets:
  N1: Part1.A0, J1.pin3
  N2: Part1.A1, J1.pin4
  N3: Part1.A2, J1.pin5
  N4: Part1.D8, R8.Pin_0
  N5: Part1.D9_PWM, R9.Pin_0
  N6: Part1.D12/MISO, R7.Pin_0
  GND: Part1.GND, J1.pin2
  N7: Part1.D2, R15.Pin_0
  N8: Part1.D3_PWM, R13.Pin_0
  N9: Part1.D4, R11.Pin_0
  N10: Part1.D5_PWM, R14.Pin_0
  N11: Part1.D6_PWM, R12.Pin_0
  N12: Part1.D7, R10.Pin_0
  5V: Part1.5V, J1.pin1
  N13: R7.Pin_1, LED3.common_cathode
  N14: R8.Pin_1, LED1.common_cathode
  N15: R9.Pin_1, LED2.common_cathode
  N16: LED1.red_anode, LED2.red_anode, LED3.red_anode
  N17: LED1.green_anode, LED2.green_anode, LED3.green_anode
  N18: LED1.blue_anode, LED2.blue_anode, LED3.blue_anode
  N19: R10.Pin_1, LED5.common_cathode
  N20: LED4.red_anode, LED5.red_anode, LED6.red_anode
  N21: LED4.common_cathode, R14.Pin_1
  N22: LED4.green_anode, LED5.green_anode, LED6.green_anode
  N23: LED4.blue_anode, LED5.blue_anode, LED6.blue_anode
  N24: LED6.common_cathode, R12.Pin_1
  N25: R11.Pin_1, LED8.common_cathode
  N26: LED7.red_anode, LED8.red_anode, LED9.red_anode
  N27: LED7.common_cathode, R15.Pin_1
  N28: LED7.green_anode, LED8.green_anode, LED9.green_anode
  N29: LED7.blue_anode, LED8.blue_anode, LED9.blue_anode
  N30: LED9.common_cathode, R13.Pin_1
